// Logisim project cmos.circ as structural Verilog: 1 circuit, main circuit main
module main (
);

  Transistor transistor_1 ();  // open: in, out, gate
  Transistor transistor_2 ();  // open: in, out, gate
  Transistor #(.\type ("n")) transistor_3 ();  // open: in, out, gate
  Transistor #(.\type ("n")) transistor_4 ();  // open: in, out, gate
  Transistor transistor_5 ();  // open: in, out, gate
  Transistor #(.\type ("n")) transistor_6 ();  // open: in, out, gate
  LED led_1 ();  // open: in
endmodule
