// Logisim project labb3.circ as structural Verilog
module labb3 (
  input  q1,
  input  q0,
  input  b,
  input  a,
  output Q1_Plus,
  output Q0_Plus
);

  wire and_1_out, nand_1_out, nor_1_out, not_1_out, not_2_out, not_3_out, not_4_out, or_1_out, or_2_out;

  not not_1 (not_1_out, q0);
  nor nor_1 (nor_1_out, q1, a);
  not not_2 (not_2_out, b);
  and and_1 (and_1_out, not_2_out, a, q1);
  not not_3 (not_3_out, b);
  not not_4 (not_4_out, q1);
  or or_1 (or_1_out, q1, q0, not_3_out, a);
  and and_2 (Q0_Plus, or_1_out, nand_1_out, or_2_out);
  nand nand_1 (nand_1_out, q0, a);
  or or_2 (or_2_out, not_4_out, q0, b);
  or or_3 (Q1_Plus, not_1_out, nor_1_out, and_1_out);
endmodule
