// Logisim project labb3_v2.circ as structural Verilog
module labb3_v2 (
  input  q1,
  input  q0,
  input  b,
  input  a,
  output Q1_Plus,
  output Q0_Plus
);

  wire and_1_out, and_2_out, clock_1_out, d_ff_1_q, d_ff_2_q, d_ff_2_qn, nand_1_out, nand_2_out, nor_1_out,
       nor_2_out, nor_3_out, nor_4_out, not_1_out, not_2_out, or_1_out, or_3_out;

  not not_1 (not_1_out, b);
  or or_1 (or_1_out, d_ff_1_q, a);
  and and_1 (and_1_out, not_1_out, a, d_ff_1_q);
  nand nand_1 (nand_1_out, d_ff_2_q, a);
  and and_2 (and_2_out, d_ff_1_q, d_ff_2_qn, not_1_out);
  nand nand_2 (nand_2_out, d_ff_2_q, or_1_out);
  nor nor_1 (nor_1_out, nor_2_out, nor_2_out);
  nor nor_2 (nor_2_out, d_ff_1_q, d_ff_2_q);
  nor nor_3 (nor_3_out, not_1_out, a);
  nor nor_4 (nor_4_out, nor_3_out, nor_3_out);
  not not_2 (not_2_out, and_2_out);
  or or_2 (Q1_Plus, nand_2_out, and_1_out);
  or or_3 (or_3_out, nor_1_out, nor_4_out);
  Clock clock_1 (.out(clock_1_out));
  and and_3 (Q0_Plus, or_3_out, nand_1_out, not_2_out);
  D_Flip_Flop d_ff_1 (.clk(clock_1_out), .D(Q1_Plus), .Q(d_ff_1_q));  // open: Qn, preset, en, reset
  D_Flip_Flop d_ff_2 (.clk(clock_1_out), .D(Q0_Plus), .Q(d_ff_2_q), .Qn(d_ff_2_qn));  // open: preset, en, reset
endmodule
