// Logisim project minKretsBYMD.circ as structural Verilog: 1 circuit, main circuit main
module main (
  input  q3,
  input  q2,
  input  q1,
  input  q0,
  output y
);

  wire and_1_out, and_2_out, and_3_out, and_4_out, and_5_out, not_1_out, not_2_out, not_3_out, not_4_out,
       or_1_out, or_2_out, or_3_out;

  not not_1 (not_1_out, q0);
  not not_2 (not_2_out, q3);
  not not_3 (not_3_out, q2);
  not not_4 (not_4_out, q1);
  and and_1 (and_1_out, not_2_out, not_3_out, q1, not_1_out);
  and and_2 (and_2_out, not_2_out, q2, not_4_out, q0);
  and and_3 (and_3_out, q3, not_3_out, not_4_out);
  and and_4 (and_4_out, q3, not_4_out, not_1_out);
  and and_5 (and_5_out, q3, q1, q0);
  or or_1 (or_1_out, and_1_out, and_2_out);
  or or_2 (or_2_out, or_1_out, and_3_out);
  or or_3 (or_3_out, and_4_out, and_5_out);
  or or_4 (y, or_2_out, or_3_out);
endmodule
